// Logisim project CONTADOR alunos4.circ as structural Verilog: 8 circuits, main circuit main
module main (
);

  wire n0_2_horas_1__24_horas, n0_2_horas_1_a, n0_2_horas_1_b, n0_2_horas_1_c, n0_2_horas_1_d,
       n0_2_horas_1_e, n0_2_horas_1_f, n0_2_horas_1_g, n0_4_horas_1_a, n0_4_horas_1_b, n0_4_horas_1_c,
       n0_4_horas_1_clock_saida, n0_4_horas_1_d, n0_4_horas_1_e, n0_4_horas_1_f, n0_4_horas_1_g,
       n0_5_minuto_1_a, n0_5_minuto_1_b, n0_5_minuto_1_c, n0_5_minuto_1_clock_de_saida, n0_5_minuto_1_d,
       n0_5_minuto_1_e, n0_5_minuto_1_f, n0_5_minuto_1_g, n0_5_segundo_1_a, n0_5_segundo_1_b,
       n0_5_segundo_1_c, n0_5_segundo_1_clock_de_saida, n0_5_segundo_1_d, n0_5_segundo_1_e, n0_5_segundo_1_f,
       n0_5_segundo_1_g, n0_9_minutos_1_a, n0_9_minutos_1_b, n0_9_minutos_1_c, n0_9_minutos_1_clock_de_saida,
       n0_9_minutos_1_d, n0_9_minutos_1_e, n0_9_minutos_1_f, n0_9_minutos_1_g, n0_9_segundo_1_a,
       n0_9_segundo_1_b, n0_9_segundo_1_c, n0_9_segundo_1_clock_de_saida, n0_9_segundo_1_d, n0_9_segundo_1_e,
       n0_9_segundo_1_f, n0_9_segundo_1_g;

  _0_4_Horas u_0_4_horas_1 (
    .Clock_saida(n0_4_horas_1_clock_saida), ._24_horas(n0_2_horas_1__24_horas),
    .clock_entrada(n0_5_minuto_1_clock_de_saida), .a(n0_4_horas_1_a), .b(n0_4_horas_1_b), .c(n0_4_horas_1_c),
    .d(n0_4_horas_1_d), .e(n0_4_horas_1_e), .f(n0_4_horas_1_f), .g(n0_4_horas_1_g));
  _0_2_Horas u_0_2_horas_1 (
    ._24_horas(n0_2_horas_1__24_horas), .clock_entrada(n0_4_horas_1_clock_saida), .a(n0_2_horas_1_a),
    .b(n0_2_horas_1_b), .c(n0_2_horas_1_c), .d(n0_2_horas_1_d), .e(n0_2_horas_1_e), .f(n0_2_horas_1_f),
    .g(n0_2_horas_1_g));
  _7_Segment_Display u_7_segment_display_1 (
    .g(n0_2_horas_1_a), .f(n0_2_horas_1_b), .a(n0_2_horas_1_c), .b(n0_2_horas_1_d), .e(n0_2_horas_1_e),
    .d(n0_2_horas_1_f), .c(n0_2_horas_1_g));  // open: dp
  _7_Segment_Display u_7_segment_display_2 (
    .g(n0_4_horas_1_a), .f(n0_4_horas_1_b), .a(n0_4_horas_1_c), .b(n0_4_horas_1_d), .e(n0_4_horas_1_e),
    .d(n0_4_horas_1_f), .c(n0_4_horas_1_g));  // open: dp
  _0_9_Minutos u_0_9_minutos_1 (
    .Clock_De_Saida(n0_9_minutos_1_clock_de_saida), .Clock_de_Entrada(n0_5_segundo_1_clock_de_saida),
    .a(n0_9_minutos_1_a), .b(n0_9_minutos_1_b), .c(n0_9_minutos_1_c), .d(n0_9_minutos_1_d),
    .e(n0_9_minutos_1_e), .f(n0_9_minutos_1_f), .g(n0_9_minutos_1_g));
  _0_5_Minuto u_0_5_minuto_1 (
    .Clock_De_Saida(n0_5_minuto_1_clock_de_saida), .Clock_De_Entrada(n0_9_minutos_1_clock_de_saida),
    .a(n0_5_minuto_1_a), .b(n0_5_minuto_1_b), .c(n0_5_minuto_1_c), .d(n0_5_minuto_1_d), .e(n0_5_minuto_1_e),
    .f(n0_5_minuto_1_f), .g(n0_5_minuto_1_g));
  _7_Segment_Display u_7_segment_display_3 (
    .g(n0_5_minuto_1_a), .f(n0_5_minuto_1_b), .a(n0_5_minuto_1_c), .b(n0_5_minuto_1_d), .e(n0_5_minuto_1_e),
    .d(n0_5_minuto_1_f), .c(n0_5_minuto_1_g));  // open: dp
  _0_5_Segundo u_0_5_segundo_1 (
    .Clock_De_Saida(n0_5_segundo_1_clock_de_saida), .Clock_De_entrada(n0_9_segundo_1_clock_de_saida),
    .a(n0_5_segundo_1_a), .b(n0_5_segundo_1_b), .c(n0_5_segundo_1_c), .d(n0_5_segundo_1_d),
    .e(n0_5_segundo_1_e), .f(n0_5_segundo_1_f), .g(n0_5_segundo_1_g));
  _7_Segment_Display u_7_segment_display_4 (
    .g(n0_9_minutos_1_a), .f(n0_9_minutos_1_b), .a(n0_9_minutos_1_c), .b(n0_9_minutos_1_d),
    .e(n0_9_minutos_1_e), .d(n0_9_minutos_1_f), .c(n0_9_minutos_1_g));  // open: dp
  _0_9_Segundo u_0_9_segundo_1 (
    .Clock_de_Saida(n0_9_segundo_1_clock_de_saida), .a(n0_9_segundo_1_a), .b(n0_9_segundo_1_b),
    .c(n0_9_segundo_1_c), .d(n0_9_segundo_1_d), .e(n0_9_segundo_1_e), .f(n0_9_segundo_1_f),
    .g(n0_9_segundo_1_g));
  _7_Segment_Display u_7_segment_display_5 (
    .g(n0_5_segundo_1_a), .f(n0_5_segundo_1_b), .a(n0_5_segundo_1_c), .b(n0_5_segundo_1_d),
    .e(n0_5_segundo_1_e), .d(n0_5_segundo_1_f), .c(n0_5_segundo_1_g));  // open: dp
  _7_Segment_Display u_7_segment_display_6 (
    .g(n0_9_segundo_1_a), .f(n0_9_segundo_1_b), .a(n0_9_segundo_1_c), .b(n0_9_segundo_1_d),
    .e(n0_9_segundo_1_e), .d(n0_9_segundo_1_f), .c(n0_9_segundo_1_g));  // open: dp
endmodule

module BCD (
  input  in_1,
  input  in_2,
  input  in_3,
  input  in_4,
  output a,
  output b,
  output c,
  output d,
  output e,
  output f,
  output g
);

  wire and_1_out, and_2_out, and_3_out, and_4_out, and_5_out, and_6_out, and_7_out, and_8_out, and_9_out,
       and_10_out, and_11_out, and_12_out, and_13_out, not_1_out, not_2_out, not_3_out, not_4_out, not_5_out,
       not_6_out, not_7_out, not_8_out, not_9_out, not_10_out, not_11_out, not_12_out, not_13_out,
       not_14_out, not_15_out, not_16_out, not_17_out, not_18_out, or_1_out, xor_1_out;

  not not_1 (not_1_out, in_4);
  not not_2 (not_2_out, in_4);
  xor xor_1 (xor_1_out, in_3, in_2);
  and and_1 (and_1_out, not_1_out, in_3);
  not not_3 (not_3_out, in_3);
  and and_2 (and_2_out, not_3_out, in_2);
  not not_4 (not_4_out, in_4);
  and and_3 (and_3_out, not_4_out, not_5_out);
  not not_5 (not_5_out, in_3);
  not not_6 (not_6_out, in_4);
  and and_4 (and_4_out, not_6_out, in_2);
  and and_5 (and_5_out, in_4, in_2);
  and and_6 (and_6_out, in_4, in_3);
  not not_7 (not_7_out, in_4);
  and and_7 (and_7_out, not_7_out, not_8_out);
  not not_8 (not_8_out, in_2);
  not not_9 (not_9_out, in_3);
  and and_8 (and_8_out, not_9_out, not_10_out);
  not not_10 (not_10_out, in_4);
  and and_9 (and_9_out, in_4, in_3);
  or or_1 (or_1_out, in_3, not_11_out);
  not not_11 (not_11_out, in_2);
  and and_10 (and_10_out, not_2_out, in_3);
  not not_12 (not_12_out, in_4);
  and and_11 (and_11_out, not_12_out, not_13_out);
  not not_13 (not_13_out, in_2);
  and and_12 (and_12_out, in_3, not_14_out);
  not not_14 (not_14_out, in_2);
  not not_15 (not_15_out, in_3);
  and and_13 (and_13_out, in_4, not_15_out, in_2);
  not not_16 (not_16_out, in_2);
  not not_17 (not_17_out, in_4);
  or or_2 (a, xor_1_out, and_1_out, in_1);
  or or_3 (b, in_1, and_2_out, and_3_out, and_4_out);
  or or_4 (c, in_1, and_5_out, and_6_out, and_7_out, and_7_out);
  or or_5 (d, in_1, not_16_out, and_8_out, and_9_out);
  and and_14 (e, not_17_out, or_1_out);
  not not_18 (not_18_out, in_3);
  or or_6 (f, and_10_out, and_11_out, and_12_out, and_13_out);
  or or_7 (g, in_4, not_18_out, in_2, in_1);
endmodule

module _0_9_Segundo (
  output Clock_de_Saida,
  output a,
  output b,
  output c,
  output d,
  output e,
  output f,
  output g
);

  wire clock_1_out, j_k_ff_1_q, j_k_ff_1_qn, j_k_ff_2_q, j_k_ff_2_qn, j_k_ff_3_q, j_k_ff_3_qn, j_k_ff_4_q;

  Clock clock_1 (.out(clock_1_out));
  J_K_Flip_Flop j_k_ff_1 (
    .J(1'b1), .clk(clock_1_out), .K(1'b1), .Q(j_k_ff_1_q), .Qn(j_k_ff_1_qn), .reset(Clock_de_Saida));  // open: preset, en
  and and_1 (Clock_de_Saida, j_k_ff_4_q, j_k_ff_2_q);
  J_K_Flip_Flop j_k_ff_2 (
    .J(1'b1), .clk(j_k_ff_1_qn), .K(1'b1), .Q(j_k_ff_2_q), .Qn(j_k_ff_2_qn), .reset(Clock_de_Saida));  // open: preset, en
  J_K_Flip_Flop j_k_ff_3 (
    .J(1'b1), .clk(j_k_ff_2_qn), .K(1'b1), .Q(j_k_ff_3_q), .Qn(j_k_ff_3_qn), .reset(Clock_de_Saida));  // open: preset, en
  J_K_Flip_Flop j_k_ff_4 (
    .J(1'b1), .clk(j_k_ff_3_qn), .K(1'b1), .Q(j_k_ff_4_q), .reset(Clock_de_Saida));  // open: Qn, preset, en
  BCD bcd_1 (
    .in_1(j_k_ff_4_q), .in_2(j_k_ff_3_q), .in_3(j_k_ff_2_q), .in_4(j_k_ff_1_q), .a(a), .b(b), .c(c), .d(d),
    .e(e), .f(f), .g(g));
endmodule

module _0_5_Segundo (
  input  Clock_De_entrada,
  output Clock_De_Saida,
  output a,
  output b,
  output c,
  output d,
  output e,
  output f,
  output g
);

  wire j_k_ff_1_q, j_k_ff_1_qn, j_k_ff_2_q, j_k_ff_2_qn, j_k_ff_3_q, j_k_ff_3_qn, j_k_ff_4_q;

  J_K_Flip_Flop j_k_ff_1 (
    .J(1'b1), .clk(Clock_De_entrada), .K(1'b1), .Q(j_k_ff_1_q), .Qn(j_k_ff_1_qn), .reset(Clock_De_Saida));  // open: preset, en
  and and_1 (Clock_De_Saida, j_k_ff_3_q, j_k_ff_2_q);
  J_K_Flip_Flop j_k_ff_2 (
    .J(1'b1), .clk(j_k_ff_1_qn), .K(1'b1), .Q(j_k_ff_2_q), .Qn(j_k_ff_2_qn), .reset(Clock_De_Saida));  // open: preset, en
  J_K_Flip_Flop j_k_ff_3 (
    .J(1'b1), .clk(j_k_ff_2_qn), .K(1'b1), .Q(j_k_ff_3_q), .Qn(j_k_ff_3_qn), .reset(Clock_De_Saida));  // open: preset, en
  J_K_Flip_Flop j_k_ff_4 (
    .J(1'b1), .clk(j_k_ff_3_qn), .K(1'b1), .Q(j_k_ff_4_q), .reset(Clock_De_Saida));  // open: Qn, preset, en
  BCD bcd_1 (
    .in_1(j_k_ff_4_q), .in_2(j_k_ff_3_q), .in_3(j_k_ff_2_q), .in_4(j_k_ff_1_q), .a(a), .b(b), .c(c), .d(d),
    .e(e), .f(f), .g(g));
endmodule

module _0_9_Minutos (
  input  Clock_de_Entrada,
  output Clock_De_Saida,
  output a,
  output b,
  output c,
  output d,
  output e,
  output f,
  output g
);

  wire j_k_ff_1_q, j_k_ff_1_qn, j_k_ff_2_q, j_k_ff_2_qn, j_k_ff_3_q, j_k_ff_3_qn, j_k_ff_4_q;

  J_K_Flip_Flop j_k_ff_1 (
    .J(1'b1), .clk(Clock_de_Entrada), .K(1'b1), .Q(j_k_ff_1_q), .Qn(j_k_ff_1_qn), .reset(Clock_De_Saida));  // open: preset, en
  and and_1 (Clock_De_Saida, j_k_ff_4_q, j_k_ff_2_q);
  J_K_Flip_Flop j_k_ff_2 (
    .J(1'b1), .clk(j_k_ff_1_qn), .K(1'b1), .Q(j_k_ff_2_q), .Qn(j_k_ff_2_qn), .reset(Clock_De_Saida));  // open: preset, en
  J_K_Flip_Flop j_k_ff_3 (
    .J(1'b1), .clk(j_k_ff_2_qn), .K(1'b1), .Q(j_k_ff_3_q), .Qn(j_k_ff_3_qn), .reset(Clock_De_Saida));  // open: preset, en
  J_K_Flip_Flop j_k_ff_4 (
    .J(1'b1), .clk(j_k_ff_3_qn), .K(1'b1), .Q(j_k_ff_4_q), .reset(Clock_De_Saida));  // open: Qn, preset, en
  BCD bcd_1 (
    .in_1(j_k_ff_4_q), .in_2(j_k_ff_3_q), .in_3(j_k_ff_2_q), .in_4(j_k_ff_1_q), .a(a), .b(b), .c(c), .d(d),
    .e(e), .f(f), .g(g));
endmodule

module _0_5_Minuto (
  input  Clock_De_Entrada,
  output Clock_De_Saida,
  output a,
  output b,
  output c,
  output d,
  output e,
  output f,
  output g
);

  wire j_k_ff_1_q, j_k_ff_1_qn, j_k_ff_2_q, j_k_ff_2_qn, j_k_ff_3_q, j_k_ff_3_qn, j_k_ff_4_q;

  J_K_Flip_Flop j_k_ff_1 (
    .J(1'b1), .clk(Clock_De_Entrada), .K(1'b1), .Q(j_k_ff_1_q), .Qn(j_k_ff_1_qn), .reset(Clock_De_Saida));  // open: preset, en
  and and_1 (Clock_De_Saida, j_k_ff_3_q, j_k_ff_2_q);
  J_K_Flip_Flop j_k_ff_2 (
    .J(1'b1), .clk(j_k_ff_1_qn), .K(1'b1), .Q(j_k_ff_2_q), .Qn(j_k_ff_2_qn), .reset(Clock_De_Saida));  // open: preset, en
  J_K_Flip_Flop j_k_ff_3 (
    .J(1'b1), .clk(j_k_ff_2_qn), .K(1'b1), .Q(j_k_ff_3_q), .Qn(j_k_ff_3_qn), .reset(Clock_De_Saida));  // open: preset, en
  J_K_Flip_Flop j_k_ff_4 (
    .J(1'b1), .clk(j_k_ff_3_qn), .K(1'b1), .Q(j_k_ff_4_q), .reset(Clock_De_Saida));  // open: Qn, preset, en
  BCD bcd_1 (
    .in_1(j_k_ff_4_q), .in_2(j_k_ff_3_q), .in_3(j_k_ff_2_q), .in_4(j_k_ff_1_q), .a(a), .b(b), .c(c), .d(d),
    .e(e), .f(f), .g(g));
endmodule

module _0_4_Horas (
  input  _24_horas,
  input  clock_entrada,
  output Clock_saida,
  output a,
  output b,
  output c,
  output d,
  output e,
  output f,
  output g
);

  wire and_1_out, and_2_out, j_k_ff_1_q, j_k_ff_1_qn, j_k_ff_2_q, j_k_ff_2_qn, j_k_ff_3_q, j_k_ff_3_qn,
       j_k_ff_4_q, not_1_out, not_2_out;

  or or_1 (Clock_saida, and_2_out, and_1_out);
  J_K_Flip_Flop j_k_ff_1 (
    .J(1'b1), .clk(clock_entrada), .K(1'b1), .Q(j_k_ff_1_q), .Qn(j_k_ff_1_qn), .reset(Clock_saida));  // open: preset, en
  and and_1 (and_1_out, j_k_ff_4_q, j_k_ff_2_q);
  J_K_Flip_Flop j_k_ff_2 (
    .J(1'b1), .clk(j_k_ff_1_qn), .K(1'b1), .Q(j_k_ff_2_q), .Qn(j_k_ff_2_qn), .reset(Clock_saida));  // open: preset, en
  J_K_Flip_Flop j_k_ff_3 (
    .J(1'b1), .clk(j_k_ff_2_qn), .K(1'b1), .Q(j_k_ff_3_q), .Qn(j_k_ff_3_qn), .reset(Clock_saida));  // open: preset, en
  J_K_Flip_Flop j_k_ff_4 (
    .J(1'b1), .clk(j_k_ff_3_qn), .K(1'b1), .Q(j_k_ff_4_q), .reset(Clock_saida));  // open: Qn, preset, en
  not not_1 (not_1_out, j_k_ff_1_q);
  not not_2 (not_2_out, j_k_ff_2_q);
  BCD bcd_1 (
    .in_1(j_k_ff_4_q), .in_2(j_k_ff_3_q), .in_3(j_k_ff_2_q), .in_4(j_k_ff_1_q), .a(a), .b(b), .c(c), .d(d),
    .e(e), .f(f), .g(g));
  and and_2 (and_2_out, not_1_out, not_2_out, j_k_ff_3_q, _24_horas);
endmodule

module _0_2_Horas (
  input  clock_entrada,
  output _24_horas,
  output a,
  output b,
  output c,
  output d,
  output e,
  output f,
  output g
);

  wire and_2_out, j_k_ff_1_q, j_k_ff_1_qn, j_k_ff_2_q, j_k_ff_2_qn, j_k_ff_3_q, j_k_ff_3_qn, j_k_ff_4_q,
       not_1_out;

  and and_1 (_24_horas, not_1_out, j_k_ff_2_q);
  J_K_Flip_Flop j_k_ff_1 (
    .J(1'b1), .clk(clock_entrada), .K(1'b1), .Q(j_k_ff_1_q), .Qn(j_k_ff_1_qn), .reset(and_2_out));  // open: preset, en
  and and_2 (and_2_out, j_k_ff_2_q, j_k_ff_1_q);
  J_K_Flip_Flop j_k_ff_2 (
    .J(1'b1), .clk(j_k_ff_1_qn), .K(1'b1), .Q(j_k_ff_2_q), .Qn(j_k_ff_2_qn), .reset(and_2_out));  // open: preset, en
  not not_1 (not_1_out, j_k_ff_1_q);
  J_K_Flip_Flop j_k_ff_3 (
    .J(1'b1), .clk(j_k_ff_2_qn), .K(1'b1), .Q(j_k_ff_3_q), .Qn(j_k_ff_3_qn), .reset(and_2_out));  // open: preset, en
  J_K_Flip_Flop j_k_ff_4 (
    .J(1'b1), .clk(j_k_ff_3_qn), .K(1'b1), .Q(j_k_ff_4_q), .reset(and_2_out));  // open: Qn, preset, en
  BCD bcd_1 (
    .in_1(j_k_ff_4_q), .in_2(j_k_ff_3_q), .in_3(j_k_ff_2_q), .in_4(j_k_ff_1_q), .a(a), .b(b), .c(c), .d(d),
    .e(e), .f(f), .g(g));
endmodule
