// Logisim project Contador com Carga paragelo.circ as structural Verilog: 2 circuits, main circuit main
module main (
  input  in_1,
  input  in_2,
  input  in_3,
  input  in_4,
  input  in_5
);

  wire and_1_out, and_2_out, and_3_out, and_4_out, and_5_out, and_6_out, and_7_out, and_8_out, and_9_out,
       and_10_out, bcd_1_a, bcd_1_b, bcd_1_c, bcd_1_d, bcd_1_e, bcd_1_f, bcd_1_g, clock_1_out, j_k_ff_1_q,
       j_k_ff_2_q, j_k_ff_3_q, j_k_ff_4_q, not_1_out, not_2_out, not_3_out, not_4_out, not_5_out;

  Clock clock_1 (.out(clock_1_out));
  not not_1 (not_1_out, in_1);
  J_K_Flip_Flop j_k_ff_1 (
    .J(1'b1), .clk(clock_1_out), .K(1'b1), .Q(j_k_ff_1_q), .preset(and_1_out), .reset(and_2_out));  // open: Qn, en
  and and_1 (and_1_out, in_2, not_1_out);
  and and_2 (and_2_out, not_2_out, not_1_out);
  not not_2 (not_2_out, in_2);
  BCD bcd_1 (
    .in_2(j_k_ff_4_q), .in_3(j_k_ff_3_q), .in_4(j_k_ff_2_q), .in_1(j_k_ff_1_q), .a(bcd_1_a), .b(bcd_1_b),
    .c(bcd_1_c), .d(bcd_1_d), .e(bcd_1_e), .f(bcd_1_f), .g(bcd_1_g));
  J_K_Flip_Flop j_k_ff_2 (
    .J(j_k_ff_1_q), .clk(clock_1_out), .K(j_k_ff_1_q), .Q(j_k_ff_2_q), .preset(and_3_out), .reset(and_5_out));  // open: Qn, en
  and and_3 (and_3_out, in_3, not_1_out);
  not not_3 (not_3_out, in_3);
  and and_4 (and_4_out, j_k_ff_1_q, j_k_ff_2_q);
  and and_5 (and_5_out, not_3_out, not_1_out);
  _7_Segment_Display u_7_segment_display_1 (
    .g(bcd_1_a), .f(bcd_1_b), .a(bcd_1_c), .b(bcd_1_d), .e(bcd_1_e), .d(bcd_1_f), .c(bcd_1_g));  // open: dp
  J_K_Flip_Flop j_k_ff_3 (
    .J(and_4_out), .clk(clock_1_out), .K(and_4_out), .Q(j_k_ff_3_q), .preset(and_6_out), .reset(and_7_out));  // open: Qn, en
  and and_6 (and_6_out, in_4, not_1_out);
  and and_7 (and_7_out, not_4_out, not_1_out);
  not not_4 (not_4_out, in_4);
  and and_8 (and_8_out, and_4_out, j_k_ff_3_q);
  J_K_Flip_Flop j_k_ff_4 (
    .J(and_8_out), .clk(clock_1_out), .K(and_8_out), .Q(j_k_ff_4_q), .preset(and_10_out), .reset(and_9_out));  // open: Qn, en
  and and_9 (and_9_out, not_5_out, not_1_out);
  and and_10 (and_10_out, in_5, not_1_out);
  not not_5 (not_5_out, in_5);
endmodule

module BCD (
  input  in_1,
  input  in_2,
  input  in_3,
  input  in_4,
  output a,
  output b,
  output c,
  output d,
  output e,
  output f,
  output g
);

  wire and_1_out, and_2_out, and_3_out, and_4_out, and_5_out, and_6_out, and_7_out, and_8_out, and_9_out,
       and_10_out, and_11_out, and_12_out, and_13_out, not_1_out, not_2_out, not_3_out, not_4_out, not_5_out,
       not_6_out, not_7_out, not_8_out, not_9_out, not_10_out, not_11_out, not_12_out, not_13_out,
       not_14_out, not_15_out, not_16_out, not_17_out, not_18_out, or_1_out, xor_1_out;

  not not_1 (not_1_out, in_1);
  not not_2 (not_2_out, in_1);
  xor xor_1 (xor_1_out, in_4, in_3);
  and and_1 (and_1_out, not_1_out, in_4);
  not not_3 (not_3_out, in_4);
  and and_2 (and_2_out, not_3_out, in_3);
  not not_4 (not_4_out, in_1);
  and and_3 (and_3_out, not_4_out, not_5_out);
  not not_5 (not_5_out, in_4);
  not not_6 (not_6_out, in_1);
  and and_4 (and_4_out, not_6_out, in_3);
  and and_5 (and_5_out, in_1, in_3);
  and and_6 (and_6_out, in_1, in_4);
  not not_7 (not_7_out, in_1);
  and and_7 (and_7_out, not_7_out, not_8_out);
  not not_8 (not_8_out, in_3);
  not not_9 (not_9_out, in_4);
  and and_8 (and_8_out, not_9_out, not_10_out);
  not not_10 (not_10_out, in_1);
  and and_9 (and_9_out, in_1, in_4);
  or or_1 (or_1_out, in_4, not_11_out);
  not not_11 (not_11_out, in_3);
  and and_10 (and_10_out, not_2_out, in_4);
  not not_12 (not_12_out, in_1);
  and and_11 (and_11_out, not_12_out, not_13_out);
  not not_13 (not_13_out, in_3);
  and and_12 (and_12_out, in_4, not_14_out);
  not not_14 (not_14_out, in_3);
  not not_15 (not_15_out, in_4);
  and and_13 (and_13_out, in_1, not_15_out, in_3);
  not not_16 (not_16_out, in_3);
  not not_17 (not_17_out, in_1);
  or or_2 (a, xor_1_out, and_1_out, in_2);
  or or_3 (b, in_2, and_2_out, and_3_out, and_4_out);
  or or_4 (c, in_2, and_5_out, and_6_out, and_7_out, and_7_out);
  or or_5 (d, in_2, not_16_out, and_8_out, and_9_out);
  and and_14 (e, not_17_out, or_1_out);
  not not_18 (not_18_out, in_4);
  or or_6 (f, and_10_out, and_11_out, and_12_out, and_13_out);
  or or_7 (g, in_1, not_18_out, in_3, in_2);
endmodule
